// Logisim project ALU8.circ as structural Verilog: 1 circuit, main circuit main
module main (
  input  [7:0] x,
  input  [7:0] y,
  input  zx,
  input  nx,
  input  zy,
  input  ny,
  input  f,
  input  no,
  output [7:0] out_9
);

  wire [7:0] And8_out_3, multilpexor_8_bits_1_out_4, multilpexor_8_bits_2_out_4, multilpexor_8_bits_3_out_4,
       multilpexor_8_bits_4_out_4, multilpexor_8_bits_5_out_4, Not8_2_out_2, Not8_3_out_2, Not8_out_2, Sum8_s;

  Multilpexor_8_bits multilpexor_8_bits_1 (.in_1(x), .in_2({8{1'b0}}), .in_3(zx), .out_4(multilpexor_8_bits_1_out_4));
  Multilpexor_8_bits multilpexor_8_bits_2 (.in_1(y), .in_2({8{1'b0}}), .in_3(zy), .out_4(multilpexor_8_bits_2_out_4));
  Not_8_bits Not8 (.in_1(multilpexor_8_bits_1_out_4), .out_2(Not8_out_2));
  Not_8_bits Not8_2 (.in_1(multilpexor_8_bits_2_out_4), .out_2(Not8_2_out_2));
  Multilpexor_8_bits multilpexor_8_bits_3 (
    .in_1(multilpexor_8_bits_1_out_4), .in_2(Not8_out_2), .in_3(nx), .out_4(multilpexor_8_bits_3_out_4));
  Multilpexor_8_bits multilpexor_8_bits_4 (
    .in_1(multilpexor_8_bits_2_out_4), .in_2(Not8_2_out_2), .in_3(ny), .out_4(multilpexor_8_bits_4_out_4));
  And_8_bits And8 (.in_1(multilpexor_8_bits_3_out_4), .in_2(multilpexor_8_bits_4_out_4), .out_3(And8_out_3));
  Sumador_8_bits Sum8 (
    .in_1(1'b0), .x(multilpexor_8_bits_4_out_4), .y(multilpexor_8_bits_3_out_4), .s(Sum8_s));  // open: c
  Multilpexor_8_bits multilpexor_8_bits_5 (
    .in_1(And8_out_3), .in_2(Sum8_s), .in_3(f), .out_4(multilpexor_8_bits_5_out_4));
  Not_8_bits Not8_3 (.in_1(multilpexor_8_bits_5_out_4), .out_2(Not8_3_out_2));
  Multilpexor_8_bits multilpexor_8_bits_6 (
    .in_1(multilpexor_8_bits_5_out_4), .in_2(Not8_3_out_2), .in_3(no), .out_4(out_9));
endmodule
