// Logisim project ALU_Test.circ as structural Verilog: 1 circuit, main circuit main
module main (
  input  [7:0] in_1,
  input  [7:0] in_2,
  input  in_3,
  input  in_4,
  input  in_5,
  input  in_6,
  input  in_7,
  input  in_8,
  output [7:0] out_9
);

  ALU8_main main_1 (.x(in_1), .y(in_2), .out_9(out_9), .zx(in_3), .nx(in_4), .zy(in_5), .ny(in_6), .f(in_7), .no(in_8));
endmodule
