// Logisim project And8.circ as structural Verilog: 1 circuit, main circuit And 8 bits
module And_8_bits (
  input  [7:0] in_1,
  input  [7:0] in_2,
  output [7:0] out_3
);

  buf and_1 (out_3[0], in_1[0]);  // AND_Gate
  and and_2 (out_3[1], in_1[1], in_2[1]);
  and and_3 (out_3[2], in_1[2], in_2[2]);
  and and_4 (out_3[3], in_1[3], in_2[3]);
  and and_5 (out_3[4], in_1[4], in_2[4]);
  and and_6 (out_3[5], in_1[5], in_2[5]);
  and and_7 (out_3[6], in_1[6], in_2[6]);
  and and_8 (out_3[7], in_1[7], in_2[7]);
endmodule
