// Logisim project Mux8.circ as structural Verilog: 1 circuit, main circuit Multilpexor 8 bits
module Multilpexor_8_bits (
  input  [7:0] in_1,
  input  [7:0] in_2,
  input  in_3,
  output [7:0] out_4
);

  Mux2_main Mux2 (.in_1(in_1[0]), .in_2(in_2[0]), .in_3(in_3), .out_4(out_4[0]));
  Mux2_main Mux2_2 (.in_1(in_1[1]), .in_2(in_2[1]), .in_3(in_3), .out_4(out_4[1]));
  Mux2_main Mux2_3 (.in_1(in_1[2]), .in_2(in_2[2]), .in_3(in_3), .out_4(out_4[2]));
  Mux2_main Mux2_4 (.in_1(in_1[3]), .in_2(in_2[3]), .in_3(in_3), .out_4(out_4[3]));
  Mux2_main Mux2_5 (.in_1(in_1[4]), .in_2(in_2[4]), .in_3(in_3), .out_4(out_4[4]));
  Mux2_main Mux2_6 (.in_1(in_1[5]), .in_2(in_2[5]), .in_3(in_3), .out_4(out_4[5]));
  Mux2_main Mux2_7 (.in_1(in_1[6]), .in_2(in_2[6]), .in_3(in_3), .out_4(out_4[6]));
  Mux2_main Mux2_8 (.in_1(in_1[7]), .in_2(in_2[7]), .in_3(in_3), .out_4(out_4[7]));
endmodule
