// Logisim project Sumador8.circ as structural Verilog: 1 circuit, main circuit main
module main (
  input  in_1,
  input  [7:0] in_2,
  input  [7:0] in_3,
  output [7:0] out_4,
  output out_5
);

  wire Sumador_2_out_5, Sumador_3_out_5, Sumador_4_out_5, Sumador_5_out_5, Sumador_6_out_5, Sumador_7_out_5,
       Sumador_out_5;

  Sumador_main Sumador (.C(in_1), .x(in_2[0]), .y(in_3[0]), .out_4(out_4[0]), .out_5(Sumador_out_5));
  Sumador_main Sumador_2 (.C(Sumador_out_5), .x(in_2[1]), .y(in_3[1]), .out_4(out_4[1]), .out_5(Sumador_2_out_5));
  Sumador_main Sumador_3 (.C(Sumador_2_out_5), .x(in_2[2]), .y(in_3[2]), .out_4(out_4[2]), .out_5(Sumador_3_out_5));
  Sumador_main Sumador_4 (.C(Sumador_3_out_5), .x(in_2[3]), .y(in_3[3]), .out_4(out_4[3]), .out_5(Sumador_4_out_5));
  Sumador_main Sumador_5 (.C(Sumador_4_out_5), .x(in_2[4]), .y(in_3[4]), .out_4(out_4[4]), .out_5(Sumador_5_out_5));
  Sumador_main Sumador_6 (.C(Sumador_5_out_5), .x(in_2[5]), .y(in_3[5]), .out_4(out_4[5]), .out_5(Sumador_6_out_5));
  Sumador_main Sumador_7 (.C(Sumador_6_out_5), .x(in_2[6]), .y(in_3[6]), .out_4(out_4[6]), .out_5(Sumador_7_out_5));
  Sumador_main Sumador_8 (.C(Sumador_7_out_5), .x(in_2[7]), .y(in_3[7]), .out_4(out_4[7]), .out_5(out_5));
endmodule
